# Fritzing sketch Sound Detector  (saved by Fritzing 0.9.2b)
breadboards: 1

parts:
  Part1 = Arduino Uno (Rev3)
  PART1 = Sound Detector
  LED1 = LED - 5mm [color="Red (633nm)" package="5 mm [THT]"]
  LED2 = LED - 5mm [color="Yellow (592nm)" package="5 mm [THT]"]
  LED3 = LED - 5mm [color="Green (565nm)" package="5 mm [THT]"]
  R1 = Resistor [tolerance=±5% resistance=50 package=THT]
  R2 = Resistor [tolerance=±5% resistance=50 package=THT]
  R3 = Resistor [tolerance=±5% resistance=50 package=THT]
  Part2 = Arduino Uno (Rev3)

nets:
  N1: Part1.A0, PART1.AUDIO, Part2.A0
  N2: Part1.D12/MISO, LED3.anode, R3.Pin_0
  N3: Part1.D13/SCK, LED2.anode
  GND: Part1.GND, LED1.anode, R1.Pin_1, R2.Pin_1, R3.Pin_1, Part2.GND
  N4: LED1.cathode, R2.Pin_0
  N5: LED2.cathode, R1.Pin_0

custom parts:
  Sound Detector: Electret microphone with multiple outputs. - First output is the actual audio - Second output is the amplitude envelope - Third output is a binary "sound present" indication - high while sound is present, low otherwise. Visit sparkfun.com for more documentations.
